# Fritzing sketch Sketch (saved by Fritzing 0.9.3b)
breadboards: 1

parts:
  J1 = Piezo Speaker
  LED2 = LED - 5mm [color="Red (633nm)" package="5 mm [THT]"]
  LCD1 = LCD screen
  LCM1602_IIC1 = LCM1602 IIC [part_number="LCM1602 IIC" chip_label="LCM1602 IIC" package="DIP (Dual Inline) [THT]"]
  U2 = NodeMCU V1.0
  R1 = Resistor [tolerance=±5% resistance=330 package="2010 [SMD]"]
  Mod1 = KY-026 Flame Sensor Module [package="Breakout board"]
  Part1 = MQ-4
  VCC1 = Battery block 9V

nets:
  GND: J1.pin1, LED2.cathode, LCM1602_IIC1.GND, U2.GND, Part1.GND, VCC1.-
  N1: J1.pin2, U2.D8
  VSS: LCD1.VSS, LCM1602_IIC1.VSS
  VDD: LCD1.VDD, LCM1602_IIC1.VDD
  N2: LCD1.V0, LCM1602_IIC1.V0
  N3: LCD1.RS, LCM1602_IIC1.RS
  N4: LCD1.R/W, LCM1602_IIC1.RW
  N5: LCD1.E, LCM1602_IIC1.E
  N6: LCD1.DB0, LCM1602_IIC1.D0
  N7: LCD1.DB1, LCM1602_IIC1.D1
  N8: LCD1.DB2, LCM1602_IIC1.D2
  N9: LCD1.DB3, LCM1602_IIC1.D3
  N10: LCD1.DB4, LCM1602_IIC1.D4
  N11: LCD1.DB5, LCM1602_IIC1.D5
  N12: LCD1.DB6, LCM1602_IIC1.D6
  N13: LCD1.DB7, LCM1602_IIC1.D7
  N14: LCD1.LED+, LCM1602_IIC1.A
  N15: LCD1.LED-, LCM1602_IIC1.K
  VCC: LCM1602_IIC1.VCC, U2.3V3, Mod1.+, Part1.VCC
  N16: LCM1602_IIC1.SDA, U2.D2
  N17: LCM1602_IIC1.SCL, U2.D1
  N18: U2.D3, Mod1.D0
  N19: U2.D5, R1.Pin_1
  N20: U2.Vin, VCC1.+
  N21: U2.A0, Part1.AO

custom parts:
  LCM1602 IIC: I2C-Module to use a 1602 or 2004 LCD on with the wire.h libory Serial LCD Modul
  NodeMCU V1.0: ESP8266 based NodeMCU
  KY-026 Flame Sensor Module: KY-026 Flame Sensor Module reacts in the presence of fire.

// code stored in the sketch: Untitled9.ino
#include <Wire.h>
#include <LiquidCrystal_I2C.h>

// Inisialisasi LCD I2C dengan alamat 0x27
LiquidCrystal_I2C lcd(0x27, 16, 2);

// Pin definisi
const int ledHijau = D7;
const int ledMerah = D8;
const int buzzer = D6;
const int sensorApi = D3;
const int sensorGas = A0;

// Nilai ambang batas untuk sensor gas (dapat disesuaikan sesuai sensor Anda)
const int gasThreshold = 300;

void setup() {
  // Inisialisasi pin
  pinMode(ledHijau, OUTPUT);
  pinMode(ledMerah, OUTPUT);
  pinMode(buzzer, OUTPUT);
  pinMode(sensorApi, INPUT);
  pinMode(sensorGas, INPUT);

  // Inisialisasi LCD
  lcd.begin();
  lcd.backlight();
  lcd.setCursor(0, 0);
  lcd.print("Sistem Peringatan");
  delay(2000);  // Tunda 2 detik
  lcd.clear();
}

void loop() {
  // Membaca nilai sensor api
  int nilaiApi = digitalRead(sensorApi);
  // Membaca nilai sensor gas
  int nilaiGas = analogRead(sensorGas);

  // Cek apakah ada api atau gas
  if (nilaiApi == HIGH || nilaiGas > gasThreshold) {
    // Jika ada api atau gas, nyalakan LED merah dan buzzer, matikan LED hijau
    digitalWrite(ledMerah, HIGH);
    digitalWrite(ledHijau, LOW);
    digitalWrite(buzzer, HIGH);
    
    // Tampilkan peringatan di LCD
    lcd.clear();
    lcd.setCursor(0, 0);
    if (nilaiApi == HIGH) {
      lcd.print("Deteksi Api!");
    }
    if (nilaiGas > gasThreshold) {
      lcd.setCursor(0, 1);
      lcd.print("Deteksi Gas!");
    }
  } else {
    // Jika tidak ada api atau gas, nyalakan LED hijau, matikan LED merah dan buzzer
    digitalWrite(ledHijau, HIGH);
    digitalWrite(ledMerah, LOW);
    digitalWrite(buzzer, LOW);

    // Tampilkan status aman di LCD
    lcd.clear();
    lcd.setCursor(0, 0);
    lcd.print("Status: Aman");
  }

  delay(500);  // Tunda 500 ms sebelum membaca kembali
}
